// Logisim project booths multiplier.circ as structural Verilog: 11 circuits, main circuit main
module main (
  input  [23:0] M_input,
  input  [23:0] Q_input,
  input  RESET,
  output [23:0] RESULT2,
  output [23:0] RESULT1,
  output [23:0] BoothOut_1,
  output [23:0] BoothOut_2
);

  wire Clock_out, controller_1_c0, controller_1_c1, controller_1_cl_a_q_1, controller_1_dec_count,
       controller_1_load__m__q__cnt, controller_1_load_a, controller_1_shr, or_1_out, Q_1_q0,
       shift_register_2_out, shift_register_3_out;
  wire [4:0] counter_1_q;
  wire [23:0] n24_bit_alu_1_p5, shift_register_1_q23;

  controller controller_1 (
    .Clock(Clock_out), .Reset(RESET), .Q0(RESULT2[0]), .Q_1(Q_1_q0), .Count(counter_1_q),
    .Cl_A_Q_1(controller_1_cl_a_q_1), .Load__M__Q__Cnt(controller_1_load__m__q__cnt),
    .Load_A(controller_1_load_a), .C0(controller_1_c0), .C1(controller_1_c1), .SHR(controller_1_shr),
    .DEC_Count(controller_1_dec_count));
  or or_1 (or_1_out, controller_1_load__m__q__cnt, controller_1_dec_count);
  Clock Clock (.out(Clock_out));
  Counter #(.width(5), .max('h18)) counter_1 (
    .load(or_1_out), .D(5'b11011), .count(controller_1_dec_count), .Q(counter_1_q), .clk(Clock_out));  // open: carry, clr
  Shift_Register #(.length(24)) shift_register_1 (
    .shift(1'b0), .clk(Clock_out), .load(controller_1_load__m__q__cnt), .d0(M_input[23]),
    .q0(shift_register_1_q23[23]), .d1(M_input[22]), .q1(shift_register_1_q23[22]), .d2(M_input[21]),
    .q2(shift_register_1_q23[21]), .d3(M_input[20]), .q3(shift_register_1_q23[20]), .d4(M_input[19]),
    .q4(shift_register_1_q23[19]), .d5(M_input[18]), .q5(shift_register_1_q23[18]), .d6(M_input[17]),
    .q6(shift_register_1_q23[17]), .d7(M_input[16]), .q7(shift_register_1_q23[16]), .d8(M_input[15]),
    .q8(shift_register_1_q23[15]), .d9(M_input[14]), .q9(shift_register_1_q23[14]), .d10(M_input[13]),
    .q10(shift_register_1_q23[13]), .d11(M_input[12]), .q11(shift_register_1_q23[12]), .d12(M_input[11]),
    .q12(shift_register_1_q23[11]), .d13(M_input[10]), .q13(shift_register_1_q23[10]), .d14(M_input[9]),
    .q14(shift_register_1_q23[9]), .d15(M_input[8]), .q15(shift_register_1_q23[8]), .d16(M_input[7]),
    .q16(shift_register_1_q23[7]), .d17(M_input[6]), .q17(shift_register_1_q23[6]), .d18(M_input[5]),
    .q18(shift_register_1_q23[5]), .d19(M_input[4]), .q19(shift_register_1_q23[4]), .d20(M_input[3]),
    .q20(shift_register_1_q23[3]), .d21(M_input[2]), .q21(shift_register_1_q23[2]), .d22(M_input[1]),
    .q22(shift_register_1_q23[1]), .d23(M_input[0]), .q23(shift_register_1_q23[0]));  // open: in, out, clr
  Shift_Register #(.length(24)) shift_register_2 (
    .shift(controller_1_shr), .in(RESULT1[23]), .clk(Clock_out), .out(shift_register_2_out),
    .load(controller_1_load_a), .clr(controller_1_cl_a_q_1), .d0(n24_bit_alu_1_p5[23]), .q0(RESULT1[23]),
    .d1(n24_bit_alu_1_p5[22]), .q1(RESULT1[22]), .d2(n24_bit_alu_1_p5[21]), .q2(RESULT1[21]),
    .d3(n24_bit_alu_1_p5[20]), .q3(RESULT1[20]), .d4(n24_bit_alu_1_p5[19]), .q4(RESULT1[19]),
    .d5(n24_bit_alu_1_p5[18]), .q5(RESULT1[18]), .d6(n24_bit_alu_1_p5[17]), .q6(RESULT1[17]),
    .d7(n24_bit_alu_1_p5[16]), .q7(RESULT1[16]), .d8(n24_bit_alu_1_p5[15]), .q8(RESULT1[15]),
    .d9(n24_bit_alu_1_p5[14]), .q9(RESULT1[14]), .d10(n24_bit_alu_1_p5[13]), .q10(RESULT1[13]),
    .d11(n24_bit_alu_1_p5[12]), .q11(RESULT1[12]), .d12(n24_bit_alu_1_p5[11]), .q12(RESULT1[11]),
    .d13(n24_bit_alu_1_p5[10]), .q13(RESULT1[10]), .d14(n24_bit_alu_1_p5[9]), .q14(RESULT1[9]),
    .d15(n24_bit_alu_1_p5[8]), .q15(RESULT1[8]), .d16(n24_bit_alu_1_p5[7]), .q16(RESULT1[7]),
    .d17(n24_bit_alu_1_p5[6]), .q17(RESULT1[6]), .d18(n24_bit_alu_1_p5[5]), .q18(RESULT1[5]),
    .d19(n24_bit_alu_1_p5[4]), .q19(RESULT1[4]), .d20(n24_bit_alu_1_p5[3]), .q20(RESULT1[3]),
    .d21(n24_bit_alu_1_p5[2]), .q21(RESULT1[2]), .d22(n24_bit_alu_1_p5[1]), .q22(RESULT1[1]),
    .d23(n24_bit_alu_1_p5[0]), .q23(RESULT1[0]));
  Register #(.width(24)) register_1 (.D(RESULT1), .en(1'b1), .Q(BoothOut_2), .clk(Clock_out), .clr(RESET));
  Shift_Register #(.length(24)) shift_register_3 (
    .shift(controller_1_shr), .in(shift_register_2_out), .clk(Clock_out), .out(shift_register_3_out),
    .load(controller_1_load__m__q__cnt), .d0(Q_input[23]), .q0(RESULT2[23]), .d1(Q_input[22]),
    .q1(RESULT2[22]), .d2(Q_input[21]), .q2(RESULT2[21]), .d3(Q_input[20]), .q3(RESULT2[20]),
    .d4(Q_input[19]), .q4(RESULT2[19]), .d5(Q_input[18]), .q5(RESULT2[18]), .d6(Q_input[17]),
    .q6(RESULT2[17]), .d7(Q_input[16]), .q7(RESULT2[16]), .d8(Q_input[15]), .q8(RESULT2[15]),
    .d9(Q_input[14]), .q9(RESULT2[14]), .d10(Q_input[13]), .q10(RESULT2[13]), .d11(Q_input[12]),
    .q11(RESULT2[12]), .d12(Q_input[11]), .q12(RESULT2[11]), .d13(Q_input[10]), .q13(RESULT2[10]),
    .d14(Q_input[9]), .q14(RESULT2[9]), .d15(Q_input[8]), .q15(RESULT2[8]), .d16(Q_input[7]),
    .q16(RESULT2[7]), .d17(Q_input[6]), .q17(RESULT2[6]), .d18(Q_input[5]), .q18(RESULT2[5]),
    .d19(Q_input[4]), .q19(RESULT2[4]), .d20(Q_input[3]), .q20(RESULT2[3]), .d21(Q_input[2]),
    .q21(RESULT2[2]), .d22(Q_input[1]), .q22(RESULT2[1]), .d23(Q_input[0]), .q23(RESULT2[0]));  // open: clr
  // _24_bit_ALU 24_bit_alu_1: pin names not known; wires that end beside it: RESULT1, shift_register_1_q23, controller_1_c1, controller_1_c0, n24_bit_alu_1_p5
  Register #(.width(24)) register_2 (.D(RESULT2), .en(1'b1), .Q(BoothOut_1), .clk(Clock_out), .clr(RESET));
  Shift_Register #(.length(1)) Q_1 (
    .shift(controller_1_shr), .in(shift_register_3_out), .clk(Clock_out), .clr(controller_1_cl_a_q_1),
    .q0(Q_1_q0));  // open: out, load, d0
endmodule

module _4_bit_and (
  input  [3:0] A,
  input  [3:0] B,
  output [3:0] result
);

  and and_1 (result[0], A[0], B[0]);
  and and_2 (result[1], A[1], B[1]);
  and and_3 (result[2], A[2], B[2]);
  and and_4 (result[3], A[3], B[3]);
endmodule

module _4_bit_or (
  input  [3:0] A,
  input  [3:0] B,
  output [3:0] RESULT
);

  or or_1 (RESULT[0], A[0], B[0]);
  or or_2 (RESULT[1], A[1], B[1]);
  or or_3 (RESULT[2], A[2], B[2]);
  or or_4 (RESULT[3], A[3], B[3]);
endmodule

module full_adder (
  input  in_1,
  input  in_2,
  input  in_3,
  output SUM,
  output Carryout
);

  wire and_1_out, and_2_out, xor_1_out;

  and and_1 (and_1_out, in_3, in_2);
  xor xor_1 (xor_1_out, in_2, in_3);
  and and_2 (and_2_out, xor_1_out, in_1);
  or or_1 (Carryout, and_2_out, and_1_out);
  xor xor_2 (SUM, in_1, xor_1_out);
endmodule

module _4_bit_full_adder (
  input  CarryIn,
  input  [3:0] A,
  input  [3:0] B,
  output [3:0] Result,
  output CarryOut
);

  wire full_adder_1_carryout, full_adder_2_carryout, full_adder_3_carryout;

  full_adder full_adder_1 (.in_2(A[0]), .in_3(B[0]), .in_1(CarryIn), .Carryout(full_adder_1_carryout), .SUM(Result[0]));
  full_adder full_adder_2 (
    .in_2(A[1]), .in_3(B[1]), .in_1(full_adder_1_carryout), .Carryout(full_adder_2_carryout), .SUM(Result[1]));
  full_adder full_adder_3 (
    .in_2(A[2]), .in_3(B[2]), .in_1(full_adder_2_carryout), .Carryout(full_adder_3_carryout), .SUM(Result[2]));
  full_adder full_adder_4 (
    .in_2(A[3]), .in_3(B[3]), .in_1(full_adder_3_carryout), .Carryout(CarryOut), .SUM(Result[3]));
endmodule

module _2_s_complement (
  input  [3:0] B,
  input  Control,
  output [3:0] B_2
);

  wire [3:0] bit_extender_1_out;

  assign bit_extender_1_out = {{3{Control}}, Control};  // Bit_Extender bit_extender_1
  xor xor_1 (B_2[0], B[0], bit_extender_1_out[0]);
  xor xor_2 (B_2[1], B[1], bit_extender_1_out[1]);
  xor xor_3 (B_2[2], B[2], bit_extender_1_out[2]);
  xor xor_4 (B_2[3], B[3], bit_extender_1_out[3]);
endmodule

module add_sub (
  input  Control,
  input  [3:0] A,
  input  [3:0] B,
  output [3:0] Result,
  output Carry,
  output Overflow
);

  wire and_1_out, and_2_out, not_1_out, not_2_out, not_3_out, sign_out_1_signout, sign_out_2_signout,
       sign_out_3_signout;
  wire [3:0] n2_s_complement_1_b_2;

  _2_s_complement u_2_s_complement_1 (.B(B), .Control(Control), .B_2(n2_s_complement_1_b_2));
  sign_out sign_out_1 (.\input (A), .SignOut(sign_out_1_signout));
  not not_1 (not_1_out, sign_out_1_signout);
  _4_bit_full_adder u_4_bit_full_adder_1 (
    .A(A), .B(n2_s_complement_1_b_2), .CarryIn(Control), .CarryOut(Carry), .Result(Result));
  sign_out sign_out_2 (.\input (n2_s_complement_1_b_2), .SignOut(sign_out_2_signout));
  not not_2 (not_2_out, sign_out_2_signout);
  sign_out sign_out_3 (.\input (Result), .SignOut(sign_out_3_signout));
  not not_3 (not_3_out, sign_out_3_signout);
  and and_1 (and_1_out, not_3_out, sign_out_2_signout, sign_out_1_signout);
  and and_2 (and_2_out, sign_out_3_signout, not_2_out, not_1_out);
  or or_1 (Overflow, and_1_out, and_2_out);
endmodule

module sign_out (
  input  [3:0] \input ,
  output SignOut
);


  assign SignOut = \input [3];
endmodule

module _4_bit_reduced_or (
  input  [3:0] Input,
  output Overflow
);

  or or_1 (Overflow, Input[0], Input[1], Input[2], Input[3]);
endmodule

module _4Bit_ALU (
  input  control0,
  input  control1,
  input  [3:0] A,
  input  [3:0] B,
  output [3:0] Result,
  output Zerofloag,
  output NegativeFlaag,
  output CarryFlag,
  output OverflowFlag
);

  wire n4_bit_reduced_or_1_overflow;
  wire [3:0] add_sub_1_result, multiplexer_1_out, n4_bit_and_1_result, n4_bit_or_1_result;

  _4_bit_and u_4_bit_and_1 (.A(A), .B(B), .result(n4_bit_and_1_result));
  _4_bit_or u_4_bit_or_1 (.A(A), .B(B), .RESULT(n4_bit_or_1_result));
  add_sub add_sub_1 (
    .A(A), .B(B), .Control(control0), .Result(add_sub_1_result), .Carry(CarryFlag), .Overflow(OverflowFlag));
  Multiplexer #(.width(4), .enable("false")) multiplexer_1 (
    .in0(n4_bit_and_1_result), .in1(n4_bit_or_1_result), .out(multiplexer_1_out), .sel(control0));
  Multiplexer #(.width(4), .enable("false")) multiplexer_2 (
    .in0(multiplexer_1_out), .in1(add_sub_1_result), .out(Result), .sel(control1));
  sign_out sign_out_1 (.\input (Result), .SignOut(NegativeFlaag));
  _4_bit_reduced_or u_4_bit_reduced_or_1 (.Input(Result), .Overflow(n4_bit_reduced_or_1_overflow));
  not not_1 (Zerofloag, n4_bit_reduced_or_1_overflow);
endmodule

// Control\n Unit
module controller (
  input  Clock,
  input  Reset,
  input  Q0,
  input  Q_1,
  input  [4:0] Count,
  output Cl_A_Q_1,
  output Load__M__Q__Cnt,
  output Load_A,
  output C0,
  output C1,
  output SHR,
  output DEC_Count
);

  wire and_1_out, and_4_out, and_5_out, multiplexer_1_out, not_1_out, not_2_out, not_3_out, not_4_out,
       not_5_out, not_6_out, not_7_out, or_2_out;
  wire [1:0] rom_1_data;
  wire [2:0] and_2_out, and_3_out, bit_extender_1_out, bit_extender_2_out, bit_extender_3_out, counter_1_q,
       or_1_out, rom_1_data_2;

  assign bit_extender_1_out = {{2{and_1_out}}, and_1_out};  // Bit_Extender bit_extender_1
  and and_1 (and_1_out, not_2_out, Q_1);
  not not_1 (not_1_out, and_1_out);
  assign and_2_out = 3'b100 & bit_extender_3_out & bit_extender_1_out;  // AND_Gate and_2, 3 bits wide
  assign or_1_out = and_2_out | rom_1_data_2 | and_3_out;  // OR_Gate or_1, 3 bits wide
  not not_2 (not_2_out, Q0);
  assign bit_extender_2_out = {{2{not_1_out}}, not_1_out};  // Bit_Extender bit_extender_2
  assign and_3_out = bit_extender_2_out & bit_extender_3_out & 3'b101;  // AND_Gate and_3, 3 bits wide
  Counter #(.width(3), .max('h7)) counter_1 (
    .load(not_5_out), .D(or_1_out), .count(multiplexer_1_out), .Q(counter_1_q), .clk(Clock), .clr(Reset));  // open: carry
  assign bit_extender_3_out = {{2{and_4_out}}, and_4_out};  // Bit_Extender bit_extender_3
  and and_4 (and_4_out, not_3_out, counter_1_q[1], not_4_out);
  not not_3 (not_3_out, counter_1_q[2]);
  not not_4 (not_4_out, counter_1_q[0]);
  not not_5 (not_5_out, multiplexer_1_out);
  Multiplexer #(.select(2), .enable("false")) multiplexer_1 (
    .in0(1'b0), .in1(1'b1), .in2(and_5_out), .in3(not_7_out), .out(multiplexer_1_out), .sel(rom_1_data));
  and and_5 (and_5_out, not_6_out, Q0);
  ROM #(.addrWidth(3), .dataWidth(12)) rom_1 (
    .addr(counter_1_q),
    .data({Cl_A_Q_1, Load__M__Q__Cnt, Load_A, C0, C1, SHR, DEC_Count, rom_1_data_2, rom_1_data}));  // open: sel
  not not_6 (not_6_out, Q_1);
  not not_7 (not_7_out, or_2_out);
  or or_2 (or_2_out, Count[0], Count[1], Count[2], Count[3], Count[4]);

  // Notes on the sheet:
  //   Control Word Format: Clear (A, Q-1), Load (M, Q, Cnt), Load A, C0, C1, Shr, Dec Cnt, Address bits (3 bit), Selection bits (2 bit)
  //   contents of rom_1 (hex, n*v repeats v):
  //   1 1 2 f94 f81 61 b 18
endmodule
